# Fritzing sketch PowerMonitor (saved by Fritzing 0.9.4)

parts:
  WeMos_D1_Mini1 = WeMos D1 Mini
  Part1 = BME280 Breakout
  R1 = Resistor [tolerance=±5% resistance=1k package="0805 [SMD]"]
  R2 = Resistor [tolerance=±5% resistance=1k package="0805 [SMD]"]
  5v_Power_Supply = Power plug
  D1 = LTE-302 [package=lte-302]

nets:
  3V3: WeMos_D1_Mini1.3V3, Part1.3.3V
  N1: WeMos_D1_Mini1.A0, R1.Pin_1
  N2: WeMos_D1_Mini1.D1, Part1.SDI/SDA
  N3: WeMos_D1_Mini1.D2, Part1.SCK/SCL
  GND: WeMos_D1_Mini1.G, Part1.GND, R2.Pin_1, 5v_Power_Supply.GND
  N4: R1.Pin_0, 5v_Power_Supply.VCC, D1.A
  N5: R2.Pin_0, D1.C
